# Fritzing sketch Schema (saved by Fritzing 0.9.3b)

parts:
  WeMos_D1_Mini1 = WeMos D1 Mini
  LED1 = RGB LED (com. anode, rbg) [package="5 mm [THT]"]
  HLK-PM1 = HLK-PM01
  R2 = Resistor [tolerance=±5% resistance=220 package="0805 [SMD]"]

nets:
  N1: WeMos_D1_Mini1.3V3, R2.Pin_0
  N2: WeMos_D1_Mini1.5V, HLK-PM1.+Vo
  N3: WeMos_D1_Mini1.D6, LED1.green_cathode
  N4: WeMos_D1_Mini1.D7, LED1.blue_cathode
  N5: WeMos_D1_Mini1.D8, LED1.red_cathode
  N6: WeMos_D1_Mini1.G, HLK-PM1.-Vo
